// Logisim project 8bits-register.circ as structural Verilog: 1 circuit, main circuit main
module main (
);

  wire clock_1_out, d_ff_1_q, d_ff_2_q, d_ff_3_q, d_ff_4_q, d_ff_5_q, d_ff_6_q, d_ff_7_q, d_ff_8_q,
       multiplexer_1_out, multiplexer_2_out, multiplexer_3_out, multiplexer_4_out, multiplexer_5_out,
       multiplexer_6_out, multiplexer_7_out, multiplexer_8_out;

  Multiplexer multiplexer_1 (.in0(1'b0), .in1(d_ff_1_q), .out(multiplexer_1_out), .sel(1'b0));  // open: en
  Multiplexer multiplexer_2 (.in0(1'b1), .in1(d_ff_2_q), .out(multiplexer_2_out), .sel(1'b0));  // open: en
  Multiplexer multiplexer_3 (.in0(1'b0), .in1(d_ff_3_q), .out(multiplexer_3_out), .sel(1'b0));  // open: en
  Multiplexer multiplexer_4 (.in0(1'b1), .in1(d_ff_4_q), .out(multiplexer_4_out), .sel(1'b0));  // open: en
  Multiplexer multiplexer_5 (.in0(1'b1), .in1(d_ff_5_q), .out(multiplexer_5_out), .sel(1'b0));  // open: en
  Multiplexer multiplexer_6 (.in0(1'b0), .in1(d_ff_6_q), .out(multiplexer_6_out), .sel(1'b0));  // open: en
  Multiplexer multiplexer_7 (.in0(1'b1), .in1(d_ff_7_q), .out(multiplexer_7_out), .sel(1'b0));  // open: en
  Multiplexer multiplexer_8 (.in0(1'b0), .in1(d_ff_8_q), .out(multiplexer_8_out), .sel(1'b0));  // open: en
  Clock clock_1 (.out(clock_1_out));
  D_Flip_Flop d_ff_1 (.clk(clock_1_out), .D(multiplexer_1_out), .Q(d_ff_1_q));  // open: Qn, preset, en, reset
  D_Flip_Flop d_ff_2 (.clk(clock_1_out), .D(multiplexer_2_out), .Q(d_ff_2_q));  // open: Qn, preset, en, reset
  D_Flip_Flop d_ff_3 (.clk(clock_1_out), .D(multiplexer_3_out), .Q(d_ff_3_q));  // open: Qn, preset, en, reset
  D_Flip_Flop d_ff_4 (.clk(clock_1_out), .D(multiplexer_4_out), .Q(d_ff_4_q));  // open: Qn, preset, en, reset
  D_Flip_Flop d_ff_5 (.clk(clock_1_out), .D(multiplexer_5_out), .Q(d_ff_5_q));  // open: Qn, preset, en, reset
  D_Flip_Flop d_ff_6 (.clk(clock_1_out), .D(multiplexer_6_out), .Q(d_ff_6_q));  // open: Qn, preset, en, reset
  D_Flip_Flop d_ff_7 (.clk(clock_1_out), .D(multiplexer_7_out), .Q(d_ff_7_q));  // open: Qn, preset, en, reset
  D_Flip_Flop d_ff_8 (.clk(clock_1_out), .D(multiplexer_8_out), .Q(d_ff_8_q));  // open: Qn, preset, en, reset
endmodule
