// Logisim project xor.circ as structural Verilog: 1 circuit, main circuit main
module main (
  output out_1
);

  wire and_1_out, and_2_out, not_1_out, not_2_out;

  not not_1 (not_1_out, 1'b0);
  not not_2 (not_2_out, 1'b1);
  and and_1 (and_1_out, not_1_out, 1'b1);
  and and_2 (and_2_out, 1'b0, not_2_out);
  or or_1 (out_1, and_1_out, and_2_out);
endmodule
